// Logisim project SAP1_new.circ as structural Verilog: 6 circuits, main circuit main
module main (
  input  [7:0] in_1,
  input  [7:0] in_2
);

  wire AI, AO, BI, button_1_out, button_2_out, CE, clock_1_out, CO, d_ff_1_q, dipswitch_1_p1, dipswitch_2_p1,
       EO, HLT, ic_74138_1_p6, II, IO, JMP, MI, MO, not_1_out, not_2_out, not_3_out, OI, or_1_out, or_2_out,
       pull_resistor_1_node, RI, RO, S, SYS_CLK, SYS_RST, T0b, T1b, T2b, T3b, T4b, T5b, T6b, T7b;
  wire [2:0] MOP_COUNTER_q;
  wire [3:3] pull_resistor_3_node;
  wire [4:4] Program_Counter_o1_2;
  wire [6:0] Program_Counter_o1;
  wire [7:0] A_Register_o1, ADD_BUS, B_Register_o1, DATA_BUS, Instruction_Register_do1, Out_Register_o1,
       RAM_IN, RAM_o1;

  D_Flip_Flop d_ff_1 (.D(HLT), .clk(HLT), .Q(d_ff_1_q), .reset(SYS_RST));  // open: Qn, preset
  Clock clock_1 (.out(clock_1_out));
  assign SYS_CLK = not_1_out ? clock_1_out : 1'bz;  // Controlled_Buffer controlled_buffer_1
  not not_1 (not_1_out, d_ff_1_q);
  assign DATA_BUS = dipswitch_1_p1 ? in_2 : 8'bz;  // Controlled_Buffer controlled_buffer_2
  // Probe on DATA_BUS
  Button button_1 (.out(button_1_out));
  // DipSwitch #(.number(2)) dipswitch_1: pin names not known; wires that end beside it: dipswitch_1_p1
  or or_1 (or_1_out, SYS_RST, button_1_out);
  Counter #(.max('h7), .width(3)) MOP_COUNTER (
    .clr(or_1_out), .count(not_2_out), .clk(not_2_out), .Q(MOP_COUNTER_q));  // open: load, up, D, carry
  not not_2 (not_2_out, SYS_CLK);
  Button button_2 (.out(button_2_out));
  not not_3 (not_3_out, SYS_CLK);
  Pull_Resistor pull_resistor_1 (.node(pull_resistor_1_node));
  // Probe on ADD_BUS
  or or_2 (or_2_out, button_2_out, Program_Counter_o1_2[4], SYS_RST);
  // IC_74138 ic_74138_1: pin names not known; wires that end beside it: MOP_COUNTER_q[0], MOP_COUNTER_q[1], MOP_COUNTER_q[2], pull_resistor_1_node, pull_resistor_1_node, ic_74138_1_p6, T0b, T1b, T2b, T3b, T4b, T5b, T6b, T7b, MOP_COUNTER_q
  Pull_Resistor #(.pull(1)) pull_resistor_2 (.node(ic_74138_1_p6));
  assign ADD_BUS = dipswitch_2_p1 ? in_1 : 8'bz;  // Controlled_Buffer controlled_buffer_3
  // Probe on MOP_COUNTER_q
  // DipSwitch #(.number(2)) dipswitch_2: pin names not known; wires that end beside it: dipswitch_2_p1
  InstructionRegister MAR (.DI(DATA_BUS), .CLK(SYS_CLK), .LD(MI), .OE(MO), .RST(SYS_RST), .DO1(RAM_IN));  // open: DO
  Pull_Resistor pull_resistor_3 (.node(pull_resistor_3_node[3]));
  Hex_Digit_Display hex_digit_display_1 (.value({pull_resistor_3_node[3], MOP_COUNTER_q}));  // open: dp
  ProgramCounter Program_Counter (
    .RST(or_2_out), .CI(JMP), .CE(CE), .CLK(SYS_CLK), .D({4'b0000, DATA_BUS[3:0]}), .OE(CO),
    .O1({Program_Counter_o1[6:4], Program_Counter_o1_2[4], Program_Counter_o1[3:0]}), .O(DATA_BUS));
  // Probe on RAM_IN
  // Probe on RAM_o1
  MyRam RAM (.A(RAM_IN[3:0]), .WE(RI), .CLK(not_3_out), .D(DATA_BUS), .OE(RO), .O1(RAM_o1), .O(DATA_BUS));
  // Probe on DATA_BUS
  InstructionRegister Instruction_Register (
    .DI(DATA_BUS), .CLK(SYS_CLK), .LD(II), .OE(IO), .RST(SYS_RST), .DO(DATA_BUS),
    .DO1(Instruction_Register_do1));
  ROM #(.dataWidth(16)) rom_1 (
    .addr({pull_resistor_3_node[3], MOP_COUNTER_q, Instruction_Register_do1[7:4]}),
    .data({JMP, CE, CO, MI, MO, RI, RO, II, IO, AI, AO, BI, HLT, OI, S, EO}));
  // Probe on {pull_resistor_3_node[3], MOP_COUNTER_q, Instruction_Register_do1[7:4]}
  // Probe on {Program_Counter_o1[6:4], Program_Counter_o1_2[4], Program_Counter_o1[3:0]}
  // Probe on Instruction_Register_do1[3:0]
  // Probe on Instruction_Register_do1[7:4]
  Button button_3 (.out(SYS_RST));
  // Probe on {JMP, CE, CO, MI, MO, RI, RO, II, IO, AI, AO, BI, HLT, OI, S, EO}
  EightBitRegister A_Register (
    .O1(A_Register_o1), .O(DATA_BUS), .D(DATA_BUS), .RST(SYS_RST), .OE(AO), .CLK(SYS_CLK), .LD(AI));
  EightBitRegister B_Register (
    .O1(B_Register_o1), .O(DATA_BUS), .D(DATA_BUS), .RST(SYS_RST), .CLK(SYS_CLK), .LD(BI));  // open: OE
  EightBitRegister Out_Register (
    .O1(Out_Register_o1), .D(DATA_BUS), .RST(SYS_RST), .CLK(SYS_CLK), .LD(OI));  // open: O, OE
  // Probe on A_Register_o1
  // Probe on B_Register_o1
  Hex_Digit_Display hex_digit_display_2 (.value(Out_Register_o1[7:4]));  // open: dp
  Hex_Digit_Display hex_digit_display_3 (.value(Out_Register_o1[3:0]));  // open: dp
  ALU alu_1 (.S(S), .Ain(A_Register_o1), .Bin(B_Register_o1), .OE(EO), .O(DATA_BUS));  // open: Cout
  // Probe on DATA_BUS

  // Notes on the sheet:
  //   contents of rom_1 (hex, n*v repeats v):
  //   16*3000 16*4300 0 1080 204 24 8080 8 1080 1080 1080 8*0 240 4*0 210 210 420 13*0 41 43
endmodule

module EightBitRegister (
  input  CLK,
  input  LD,
  input  [7:0] D,
  input  RST,
  input  OE,
  output [7:0] O,
  output [7:0] O1
);

  wire and_1_out;

  Pull_Resistor pull_resistor_1 (.node(CLK));
  Pull_Resistor pull_resistor_2 (.node(LD));
  and and_1 (and_1_out, CLK, LD);
  D_Flip_Flop d_ff_1 (.D(D[0]), .clk(and_1_out), .Q(O1[0]), .reset(RST));  // open: Qn, preset
  Pull_Resistor pull_resistor_3 (.node(D[0]));
  D_Flip_Flop d_ff_2 (.D(D[1]), .clk(and_1_out), .Q(O1[1]), .reset(RST));  // open: Qn, preset
  Pull_Resistor pull_resistor_4 (.node(D[1]));
  D_Flip_Flop d_ff_3 (.D(D[2]), .clk(and_1_out), .Q(O1[2]), .reset(RST));  // open: Qn, preset
  Pull_Resistor pull_resistor_5 (.node(D[2]));
  D_Flip_Flop d_ff_4 (.D(D[3]), .clk(and_1_out), .Q(O1[3]), .reset(RST));  // open: Qn, preset
  Pull_Resistor pull_resistor_6 (.node(D[3]));
  D_Flip_Flop d_ff_5 (.D(D[4]), .clk(and_1_out), .Q(O1[4]), .reset(RST));  // open: Qn, preset
  Pull_Resistor pull_resistor_7 (.node(D[4]));
  D_Flip_Flop d_ff_6 (.D(D[5]), .clk(and_1_out), .Q(O1[5]), .reset(RST));  // open: Qn, preset
  Pull_Resistor pull_resistor_8 (.node(D[5]));
  D_Flip_Flop d_ff_7 (.D(D[6]), .clk(and_1_out), .Q(O1[6]), .reset(RST));  // open: Qn, preset
  Pull_Resistor pull_resistor_9 (.node(D[6]));
  D_Flip_Flop d_ff_8 (.D(D[7]), .clk(and_1_out), .Q(O1[7]), .reset(RST));  // open: Qn, preset
  Pull_Resistor pull_resistor_10 (.node(D[7]));
  Pull_Resistor pull_resistor_11 (.node(RST));
  assign O[0] = OE ? O1[0] : 1'bz;  // Controlled_Buffer controlled_buffer_1
  assign O[1] = OE ? O1[1] : 1'bz;  // Controlled_Buffer controlled_buffer_2
  assign O[2] = OE ? O1[2] : 1'bz;  // Controlled_Buffer controlled_buffer_3
  assign O[3] = OE ? O1[3] : 1'bz;  // Controlled_Buffer controlled_buffer_4
  assign O[4] = OE ? O1[4] : 1'bz;  // Controlled_Buffer controlled_buffer_5
  assign O[5] = OE ? O1[5] : 1'bz;  // Controlled_Buffer controlled_buffer_6
  assign O[6] = OE ? O1[6] : 1'bz;  // Controlled_Buffer controlled_buffer_7
  assign O[7] = OE ? O1[7] : 1'bz;  // Controlled_Buffer controlled_buffer_8
  Pull_Resistor pull_resistor_12 (.node(OE));

  // Notes on the sheet:
  //   LD = active high
  //   RST = active high
  //   OE = active high
endmodule

module ALU (
  input  S,
  input  [7:0] Ain,
  input  [7:0] Bin,
  input  OE,
  output [7:0] O,
  output Cout
);

  wire adder_1_cout, multiplexer_2_out, subtractor_1_bout;
  wire [7:0] adder_1_out, multiplexer_1_out, subtractor_1_out;

  Adder adder_1 (.a(Ain), .b(Bin), .out(adder_1_out), .cout(adder_1_cout));  // open: cin
  Subtractor subtractor_1 (.a(Ain), .b(Bin), .out(subtractor_1_out), .bout(subtractor_1_bout));  // open: bin
  Multiplexer #(.enable("false"), .width(8)) multiplexer_1 (
    .in0(adder_1_out), .in1(subtractor_1_out), .out(multiplexer_1_out), .sel(S));
  Multiplexer #(.enable("false")) multiplexer_2 (
    .in0(adder_1_cout), .in1(subtractor_1_bout), .out(multiplexer_2_out), .sel(S));
  assign O = OE ? multiplexer_1_out : 8'bz;  // Controlled_Buffer controlled_buffer_1
  Pull_Resistor pull_resistor_1 (.node(OE));
  assign Cout = OE ? multiplexer_2_out : 1'bz;  // Controlled_Buffer controlled_buffer_2
endmodule

module ProgramCounter (
  input  RST,
  input  CI,
  input  CE,
  input  CLK,
  input  [7:0] D,
  input  OE,
  output [7:0] O1,
  output [7:0] O
);

  Counter counter_1 (.clr(RST), .load(CI), .count(CE), .clk(CLK), .D(D), .Q(O1));  // open: up, carry
  assign O = OE ? O1 : 8'bz;  // Controlled_Buffer controlled_buffer_1
endmodule

module MyRam (
  input  [3:0] A,
  input  WE,
  input  CLK,
  input  [7:0] D,
  input  OE,
  output [7:0] O1,
  output [7:0] O
);

  wire not_1_out;

  not not_1 (not_1_out, WE);
  RAM #(.addrWidth(4)) ram_1 (.addr(A), .we(WE), .oe(not_1_out), .clk(CLK), .din(D), .dout(O1));
  assign O = OE ? O1 : 8'bz;  // Controlled_Buffer controlled_buffer_1
endmodule

module InstructionRegister (
  input  [7:0] DI,
  input  CLK,
  input  LD,
  input  OE,
  input  RST,
  output [7:0] DO,
  output [7:0] DO1
);

  EightBitRegister eightbitregister_1 (.O1(DO1), .O(DO), .D(DI), .RST(RST), .OE(OE), .CLK(CLK), .LD(LD));
endmodule
