// Logisim project WH01.circ as structural Verilog: 12 circuits, main circuit main
module main (
);

  wire ADI, ADO, ADRD, ADRI, AI, alu_1_cout, alu_1_g, alu_1_l, alu_1_q, and_1_out, and_2_out, and_3_out, AO,
       BE, BI, BNE, BO, button_2_out, button_3_out, BZ, CE, CF, CI, clock_1_out, CO, CRO, d_ff_1_q, EF, EO,
       FI, flagsregister_1_za, flagsregister_1_zb, GF, HLT, II, IO, io_interface_1_bo, IRI, JMP, LF, MI, MO,
       not_1_out, not_2_out, not_3_out, not_4_out, not_5_out, OI, or_1_out, or_2_out, or_3_out, or_4_out,
       OTI, pull_resistor_1_node, pull_resistor_2_node, RI, RO, S, SE, serialout_1_tx, SI, SID, SO, SOI,
       SYS_CLK, SYS_RST, TI, TRO, TX, ZS;
  wire [2:0] MOP_COUNTER_q;
  wire [3:3] pull_resistor_3_node;
  wire [7:0] A_Register_o1, alu_1_o1, B_Register_o1, C_Register_o1, io_interface_1_o1, keyboard_1_data, OR2,
       Out_Register_1_o1, stack_1_sp, TMP_Register_o1;
  wire [15:0] add_register_1_o1, Program_Counter_o1;
  wire [23:0] DATA_BUS, Instruction_Register_do1, RAM_IN, RAM_o1, stack_1_so1;
  wire [63:37] Control_Logic_data;

  Pull_Resistor #(.pull(1)) pull_resistor_1 (.node(pull_resistor_1_node));
  Button button_1 (.out(SYS_RST));
  or or_1 (or_1_out, OR2[7], SYS_RST);
  not not_1 (not_1_out, OTI);
  TTY #(.cols(64)) tty_1 (.data(OR2[6:0]), .clk(not_1_out), .we(pull_resistor_1_node), .clr(or_1_out));
  Keyboard keyboard_1 (.clk(io_interface_1_bo), .data(keyboard_1_data[6:0]));  // open: re, clr, avail
  IO_Interface io_interface_1 (
    .D(keyboard_1_data), .BI(IRI), .RST(SYS_RST), .O(DATA_BUS[7:0]), .BO(io_interface_1_bo),
    .O1(io_interface_1_o1));
  not not_2 (not_2_out, EF);
  // Probe on io_interface_1_o1
  and and_1 (and_1_out, BE, EF);
  and and_2 (and_2_out, BZ, ZS);
  and and_3 (and_3_out, BNE, not_2_out);
  Pull_Resistor pull_resistor_2 (.node(pull_resistor_2_node));
  or or_2 (or_2_out, JMP, and_1_out, pull_resistor_2_node, pull_resistor_2_node, and_2_out, and_3_out);
  Button button_2 (.out(button_2_out));
  not not_3 (not_3_out, SYS_CLK);
  Button button_3 (.out(button_3_out));
  or or_3 (or_3_out, SYS_RST, button_2_out);
  Counter #(.max('h7), .width(3)) MOP_COUNTER (
    .clr(or_3_out), .count(not_3_out), .clk(not_3_out), .Q(MOP_COUNTER_q));  // open: load, up, D, carry
  D_Flip_Flop d_ff_1 (.D(HLT), .clk(HLT), .Q(d_ff_1_q), .reset(SYS_RST));  // open: Qn, preset
  or or_4 (or_4_out, button_3_out, SYS_RST);
  not not_4 (not_4_out, SYS_CLK);
  EightBitRegister Out_Register_2 (.O1(OR2), .D(DATA_BUS[7:0]), .RST(SYS_RST), .CLK(SYS_CLK), .LD(OTI));  // open: O, OE
  EightBitRegister Out_Register_1 (
    .O1(Out_Register_1_o1), .D(DATA_BUS[7:0]), .RST(SYS_RST), .CLK(SYS_CLK), .LD(OI));  // open: O, OE
  Clock clock_1 (.out(clock_1_out));
  not not_5 (not_5_out, d_ff_1_q);
  assign SYS_CLK = not_5_out ? clock_1_out : 1'bz;  // Controlled_Buffer controlled_buffer_1
  Pull_Resistor pull_resistor_3 (.node(pull_resistor_3_node[3]));
  Hex_Digit_Display hex_digit_display_1 (.value({pull_resistor_3_node[3], MOP_COUNTER_q}));  // open: dp
  // Probe on MOP_COUNTER_q
  ProgramCounter Program_Counter (
    .RST(or_4_out), .CI(or_2_out), .CE(CE), .CLK(SYS_CLK), .D(DATA_BUS[15:0]), .OE(CO),
    .O1(Program_Counter_o1), .O(DATA_BUS[15:0]));
  InstructionRegister MAR (.DI(DATA_BUS), .CLK(SYS_CLK), .LD(MI), .OE(MO), .RST(SYS_RST), .DO1(RAM_IN));  // open: DO
  MyRam RAM (.A(RAM_IN), .WE(RI), .CLK(not_4_out), .D(DATA_BUS), .OE(RO), .O1(RAM_o1), .O(DATA_BUS));
  InstructionRegister Instruction_Register (
    .DI(DATA_BUS), .CLK(SYS_CLK), .LD(II), .OE(IO), .RST(SYS_RST), .DO(DATA_BUS),
    .DO1(Instruction_Register_do1));
  // Probe on {pull_resistor_3_node[3], MOP_COUNTER_q, Instruction_Register_do1[23:16]}
  // Probe on Program_Counter_o1
  // Probe on RAM_IN
  // Probe on RAM_o1
  // Probe on DATA_BUS
  Hex_Digit_Display hex_digit_display_2 (.value(Out_Register_1_o1[7:4]));  // open: dp
  // Probe on Instruction_Register_do1[15:0]
  // Probe on Instruction_Register_do1[23:16]
  ROM #(.addrWidth(12), .dataWidth(64)) Control_Logic (
    .addr({pull_resistor_3_node[3], MOP_COUNTER_q, Instruction_Register_do1[23:16]}),
    .data({Control_Logic_data, IRI, ADRD, ADRI, ADO, ADI, TRO, CRO, CI, TI, SID, SI, SE, SO, BZ, BNE, SOI, OTI, TX, BE, FI, BO, JMP, CE, CO, MI, MO, RI, RO, II, IO, AI, AO, BI, HLT, OI, S, EO}));
  Hex_Digit_Display hex_digit_display_3 (.value(Out_Register_1_o1[3:0]));  // open: dp
  Hex_Digit_Display hex_digit_display_4 (.value(Instruction_Register_do1[23:20]));  // open: dp
  Hex_Digit_Display hex_digit_display_5 (.value(Instruction_Register_do1[19:16]));  // open: dp
  EightBitRegister A_Register (
    .O1(A_Register_o1), .O(DATA_BUS[7:0]), .D(DATA_BUS[7:0]), .RST(SYS_RST), .OE(AO), .CLK(SYS_CLK), .LD(AI));
  EightBitRegister TMP_Register (
    .O1(TMP_Register_o1), .O(DATA_BUS[7:0]), .D(DATA_BUS[7:0]), .RST(SYS_RST), .OE(TRO), .CLK(SYS_CLK),
    .LD(TI));
  EightBitRegister B_Register (
    .O1(B_Register_o1), .O(DATA_BUS[7:0]), .D(DATA_BUS[7:0]), .RST(SYS_RST), .OE(BO), .CLK(SYS_CLK), .LD(BI));
  EightBitRegister C_Register (
    .O1(C_Register_o1), .O(DATA_BUS[7:0]), .D(DATA_BUS[7:0]), .RST(SYS_RST), .OE(CRO), .CLK(SYS_CLK), .LD(CI));
  // Probe on A_Register_o1
  // Probe on TMP_Register_o1
  // Probe on B_Register_o1
  // Probe on C_Register_o1
  Add_Register add_register_1 (
    .D(DATA_BUS[15:0]), .CLK(SYS_CLK), .LD(ADI), .OE(ADO), .RST(SYS_RST), .DEC(ADRD), .INC(ADRI),
    .O(DATA_BUS[15:0]), .O1(add_register_1_o1));
  // Probe on add_register_1_o1
  ALU alu_1 (
    .S(S), .Ain(A_Register_o1), .Bin(TMP_Register_o1), .OE(EO), .O1(alu_1_o1), .O(DATA_BUS[7:0]),
    .Cout(alu_1_cout), .G(alu_1_g), .Q(alu_1_q), .L(alu_1_l));
  FlagsRegister flagsregister_1 (
    .S(alu_1_o1), .A(A_Register_o1), .B(TMP_Register_o1), .C(alu_1_cout), .G(alu_1_g), .Q(alu_1_q),
    .L(alu_1_l), .RST(SYS_RST), .CLK(SYS_CLK), .LD(FI), .ZS(ZS), .ZA(flagsregister_1_za),
    .ZB(flagsregister_1_zb), .Co(CF), .Go(GF), .Qo(EF), .Lo(LF));
  SerialOut serialout_1 (.D(DATA_BUS[7:0]), .CLK(SYS_CLK), .LD(SOI), .RST(SYS_RST), .OE(TX), .TX(serialout_1_tx));
  Stack stack_1 (
    .RST(SYS_RST), .SID(SID), .SE(SE), .CLK(SYS_CLK), .WE(SI), .SI(DATA_BUS), .OE(SO), .SO(DATA_BUS),
    .SO1(stack_1_so1), .SP(stack_1_sp));
  // Probe on serialout_1_tx
  // Probe on stack_1_so1
  // Probe on stack_1_sp

  // Notes on the sheet:
  //   contents of Control_Logic (hex, n*v repeats v):
  //   256*3000 256*4300 0 1080 204 24 8080 8 4*1080 10004 1080 40000004 1080 40080 400080 20000 800080
  //   a000000 1000040 a000000 11000000 10040 2040 30 20000020 1080 100020 110000 1080 0 200020 400000000
  //   800000000 200001000 1080 1080 200001000 219*0 240 4*0 10000200 10000200 420 210 0 20000200 0 10400
  //   4*0 4000020 2000000 4002000 5*0 10000200 0 0 100000200 0 80000 0 0 240 1000000400 200000400 420
  //   224*0 20000 20000 12*0 8080 82008000 240*0 41 43
  //   SID 1 == Increment SP
  //   SID 0 == Decrement SP
endmodule

module EightBitRegister (
  input  CLK,
  input  LD,
  input  [7:0] D,
  input  RST,
  input  OE,
  output [7:0] O,
  output [7:0] O1
);

  wire and_1_out;

  Pull_Resistor pull_resistor_1 (.node(CLK));
  Pull_Resistor pull_resistor_2 (.node(LD));
  and and_1 (and_1_out, CLK, LD);
  D_Flip_Flop d_ff_1 (.D(D[0]), .clk(and_1_out), .Q(O1[0]), .reset(RST));  // open: Qn, preset
  Pull_Resistor pull_resistor_3 (.node(D[0]));
  D_Flip_Flop d_ff_2 (.D(D[1]), .clk(and_1_out), .Q(O1[1]), .reset(RST));  // open: Qn, preset
  Pull_Resistor pull_resistor_4 (.node(D[1]));
  D_Flip_Flop d_ff_3 (.D(D[2]), .clk(and_1_out), .Q(O1[2]), .reset(RST));  // open: Qn, preset
  Pull_Resistor pull_resistor_5 (.node(D[2]));
  D_Flip_Flop d_ff_4 (.D(D[3]), .clk(and_1_out), .Q(O1[3]), .reset(RST));  // open: Qn, preset
  Pull_Resistor pull_resistor_6 (.node(D[3]));
  D_Flip_Flop d_ff_5 (.D(D[4]), .clk(and_1_out), .Q(O1[4]), .reset(RST));  // open: Qn, preset
  Pull_Resistor pull_resistor_7 (.node(D[4]));
  D_Flip_Flop d_ff_6 (.D(D[5]), .clk(and_1_out), .Q(O1[5]), .reset(RST));  // open: Qn, preset
  Pull_Resistor pull_resistor_8 (.node(D[5]));
  D_Flip_Flop d_ff_7 (.D(D[6]), .clk(and_1_out), .Q(O1[6]), .reset(RST));  // open: Qn, preset
  Pull_Resistor pull_resistor_9 (.node(D[6]));
  D_Flip_Flop d_ff_8 (.D(D[7]), .clk(and_1_out), .Q(O1[7]), .reset(RST));  // open: Qn, preset
  Pull_Resistor pull_resistor_10 (.node(D[7]));
  Pull_Resistor pull_resistor_11 (.node(RST));
  assign O[0] = OE ? O1[0] : 1'bz;  // Controlled_Buffer controlled_buffer_1
  assign O[1] = OE ? O1[1] : 1'bz;  // Controlled_Buffer controlled_buffer_2
  assign O[2] = OE ? O1[2] : 1'bz;  // Controlled_Buffer controlled_buffer_3
  assign O[3] = OE ? O1[3] : 1'bz;  // Controlled_Buffer controlled_buffer_4
  assign O[4] = OE ? O1[4] : 1'bz;  // Controlled_Buffer controlled_buffer_5
  assign O[5] = OE ? O1[5] : 1'bz;  // Controlled_Buffer controlled_buffer_6
  assign O[6] = OE ? O1[6] : 1'bz;  // Controlled_Buffer controlled_buffer_7
  assign O[7] = OE ? O1[7] : 1'bz;  // Controlled_Buffer controlled_buffer_8
  Pull_Resistor pull_resistor_12 (.node(OE));

  // Notes on the sheet:
  //   LD = active high
  //   RST = active high
  //   OE = active high
endmodule

module ALU (
  input  S,
  input  [7:0] Ain,
  input  [7:0] Bin,
  input  OE,
  output [7:0] O1,
  output [7:0] O,
  output Cout,
  output G,
  output Q,
  output L
);

  wire adder_1_cout, subtractor_1_bout;
  wire [7:0] adder_1_out, subtractor_1_out;

  Adder adder_1 (.a(Ain), .b(Bin), .out(adder_1_out), .cout(adder_1_cout));  // open: cin
  Subtractor subtractor_1 (.a(Ain), .b(Bin), .out(subtractor_1_out), .bout(subtractor_1_bout));  // open: bin
  Comparator comparator_1 (.a(Ain), .b(Bin), .gt(G), .eq(Q), .lt(L));
  Multiplexer #(.enable("false"), .width(8)) multiplexer_1 (
    .in0(adder_1_out), .in1(subtractor_1_out), .out(O1), .sel(S));
  Multiplexer #(.enable("false")) multiplexer_2 (.in0(adder_1_cout), .in1(subtractor_1_bout), .out(Cout), .sel(S));
  assign O = OE ? O1 : 8'bz;  // Controlled_Buffer controlled_buffer_1
  Pull_Resistor pull_resistor_1 (.node(OE));
endmodule

module ProgramCounter (
  input  RST,
  input  CI,
  input  CE,
  input  CLK,
  input  [15:0] D,
  input  OE,
  output [15:0] O1,
  output [15:0] O
);

  Counter #(.max('hffff), .width(16)) counter_1 (
    .clr(RST), .load(CI), .count(CE), .clk(CLK), .D(D), .Q(O1));  // open: up, carry
  assign O = OE ? O1 : 16'bz;  // Controlled_Buffer controlled_buffer_1
endmodule

module MyRam (
  input  [23:0] A,
  input  WE,
  input  CLK,
  input  [23:0] D,
  input  OE,
  output [23:0] O1,
  output [23:0] O
);

  wire not_1_out;

  not not_1 (not_1_out, WE);
  RAM #(.addrWidth(16), .dataWidth(24)) ram_1 (.addr(A[15:0]), .we(WE), .oe(not_1_out), .clk(CLK), .din(D), .dout(O1));
  assign O = OE ? O1 : 24'bz;  // Controlled_Buffer controlled_buffer_1
endmodule

module InstructionRegister (
  input  [23:0] DI,
  input  CLK,
  input  LD,
  input  OE,
  input  RST,
  output [23:0] DO,
  output [23:0] DO1
);

  EightBitRegister eightbitregister_1 (.O1(DO1[7:0]), .O(DO[7:0]), .D(DI[7:0]), .RST(RST), .OE(OE), .CLK(CLK), .LD(LD));
  EightBitRegister eightbitregister_2 (
    .O1(DO1[15:8]), .O(DO[15:8]), .D(DI[15:8]), .RST(RST), .OE(OE), .CLK(CLK), .LD(LD));
  EightBitRegister eightbitregister_3 (
    .O1(DO1[23:16]), .O(DO[23:16]), .D(DI[23:16]), .RST(RST), .OE(OE), .CLK(CLK), .LD(LD));
endmodule

module FlagsRegister (
  input  [7:0] S,
  input  [7:0] A,
  input  [7:0] B,
  input  C,
  input  G,
  input  Q,
  input  L,
  input  RST,
  input  CLK,
  input  LD,
  output ZS,
  output ZA,
  output ZB,
  output Co,
  output Go,
  output Qo,
  output Lo
);

  wire and_1_out, comparator_1_eq, comparator_2_eq, comparator_3_eq;

  Comparator comparator_1 (.a({8{1'b0}}), .b(S), .eq(comparator_1_eq));  // open: gt, lt
  Comparator comparator_2 (.a({8{1'b0}}), .b(A), .eq(comparator_2_eq));  // open: gt, lt
  Comparator comparator_3 (.a({8{1'b0}}), .b(B), .eq(comparator_3_eq));  // open: gt, lt
  and and_1 (and_1_out, CLK, LD);
  D_Flip_Flop d_ff_1 (.D(comparator_1_eq), .clk(and_1_out), .Q(ZS), .reset(RST));  // open: Qn, preset
  D_Flip_Flop d_ff_2 (.D(comparator_2_eq), .clk(and_1_out), .Q(ZA), .reset(RST));  // open: Qn, preset
  D_Flip_Flop d_ff_3 (.D(comparator_3_eq), .clk(and_1_out), .Q(ZB), .reset(RST));  // open: Qn, preset
  D_Flip_Flop d_ff_4 (.D(C), .clk(and_1_out), .Q(Co), .reset(RST));  // open: Qn, preset
  D_Flip_Flop d_ff_5 (.D(G), .clk(and_1_out), .Q(Go), .reset(RST));  // open: Qn, preset
  D_Flip_Flop d_ff_6 (.D(Q), .clk(and_1_out), .Q(Qo), .reset(RST));  // open: Qn, preset
  D_Flip_Flop d_ff_7 (.D(L), .clk(and_1_out), .Q(Lo), .reset(RST));  // open: Qn, preset
endmodule

module Stack (
  input  RST,
  input  SID,
  input  SE,
  input  CLK,
  input  WE,
  input  [23:0] SI,
  input  OE,
  output [23:0] SO,
  output [23:0] SO1,
  output [7:0] SP
);

  wire pull_resistor_1_node;

  Pull_Resistor #(.pull(1)) pull_resistor_1 (.node(pull_resistor_1_node));
  Counter counter_1 (.clr(RST), .up(SID), .count(SE), .clk(CLK), .Q(SP));  // open: load, D, carry
  RAM #(.dataWidth(24)) ram_1 (.addr(SP), .we(WE), .oe(pull_resistor_1_node), .clk(CLK), .din(SI), .dout(SO1));
  assign SO = OE ? SO1 : 24'bz;  // Controlled_Buffer controlled_buffer_1
endmodule

module SerialOut (
  input  [7:0] D,
  input  CLK,
  input  LD,
  input  RST,
  input  OE,
  output TX
);

  wire bitselector_1_out, counter_1_carry, d_ff_1_q, pull_resistor_1_node;
  wire [2:0] counter_1_q;
  wire [7:0] eightbitregister_1_o1;

  Pull_Resistor #(.pull(1)) pull_resistor_1 (.node(pull_resistor_1_node));
  EightBitRegister eightbitregister_1 (
    .O1(eightbitregister_1_o1), .D(D), .RST(RST), .CLK(CLK), .LD(LD));  // open: O, OE
  Counter #(.max('h7), .width(3)) counter_1 (
    .clr(LD), .up(pull_resistor_1_node), .count(CLK), .clk(CLK), .carry(counter_1_carry), .Q(counter_1_q));  // open: load, D
  // Probe on eightbitregister_1_o1
  BitSelector bitselector_1 (.in(eightbitregister_1_o1), .out(bitselector_1_out), .sel(counter_1_q));
  D_Flip_Flop d_ff_1 (.D(OE), .clk(OE), .Q(d_ff_1_q), .reset(counter_1_carry));  // open: Qn, preset
  assign TX = d_ff_1_q ? bitselector_1_out : 1'bz;  // Controlled_Buffer controlled_buffer_1
  // Digital_Oscilloscope #(.nState(35)) digital_oscilloscope_1: pin names not known; wires that end beside it: CLK, TX, pull_resistor_1_node, RST
endmodule

module Add_Register (
  input  [15:0] D,
  input  CLK,
  input  LD,
  input  OE,
  input  RST,
  input  DEC,
  input  INC,
  output [15:0] O,
  output [15:0] O1
);

  wire or_1_out;
  wire [0:0] pull_resistor_1_node;
  wire [14:0] pull_resistor_2_node;
  wire [15:0] DEC_t, INC_t, multiplexer_1_out;

  or or_1 (or_1_out, LD, DEC, INC);
  Multiplexer #(.enable("false"), .select(3), .width(16)) multiplexer_1 (
    .in1(D), .in2(DEC_t), .in4(INC_t), .out(multiplexer_1_out), .sel({INC, DEC, LD}));  // open: in0, in3, in5, in6, in7
  // Probe on multiplexer_1_out
  EightBitRegister eightbitregister_1 (
    .O1(O1[7:0]), .O(O[7:0]), .D(multiplexer_1_out[7:0]), .RST(RST), .OE(OE), .CLK(CLK), .LD(or_1_out));
  EightBitRegister eightbitregister_2 (
    .O1(O1[15:8]), .O(O[15:8]), .D(multiplexer_1_out[15:8]), .RST(RST), .OE(OE), .CLK(CLK), .LD(or_1_out));
  Pull_Resistor #(.pull(1)) pull_resistor_1 (.node(pull_resistor_1_node[0]));
  Pull_Resistor pull_resistor_2 (.node(pull_resistor_2_node));
  Subtractor #(.width(16)) subtractor_1 (
    .a(O1), .b({pull_resistor_2_node, pull_resistor_1_node[0]}), .out(DEC_t));  // open: bin, bout
  Adder #(.width(16)) adder_1 (
    .a(O1), .b({pull_resistor_2_node, pull_resistor_1_node[0]}), .out(INC_t));  // open: cin, cout
endmodule

module IO_Interface (
  input  [7:0] D,
  input  BI,
  input  RST,
  output [7:0] O,
  output BO,
  output [7:0] O1
);

  EightBitRegister eightbitregister_1 (.O1(O1), .O(O), .D(D), .RST(RST), .OE(BI), .CLK(BI), .LD(BI));

  assign BO = BI;
endmodule

module BootRom (
  input  [23:0] in_1,
  input  OE,
  output [23:0] O1,
  output [23:0] O
);

  ROM #(.addrWidth(16), .dataWidth(24)) rom_1 (.addr(in_1[15:0]), .data(O1));
  assign O = OE ? O1 : 24'bz;  // Controlled_Buffer controlled_buffer_1
endmodule
